# Fritzing sketch Untitled Sketch 2 (saved by Fritzing 0.9.3b)

parts:
  L298N1 = L298N DC motor driver
  L298N2 = L298N DC motor driver
  L298N3 = L298N DC motor driver
  Composant1 = Arduino Uno (Rev3)
  Composant2 = Nextion LCD DRAFT [part_number=Nextion]
  M1 = DC Motor
  M2 = DC Motor
  M3 = DC Motor
  LED1 = smd LED [color="Red (633nm)" package="0603 [SMD]"]
  LED2 = smd LED [color="Red (633nm)" package="0603 [SMD]"]
  LED3 = smd LED [color="Red (633nm)" package="0603 [SMD]"]

nets:
  N1: L298N1.OUT1, M1.pin_2
  N2: L298N1.OUT2, M1.pin_1
  N3: L298N1.OUT3, M3.pin_2
  N4: L298N1.OUT4, M3.pin_1
  12V: L298N1.12V, L298N2.12V, L298N3.12V
  GND: L298N1.GND, L298N2.GND, L298N3.GND, Composant1.GND, Composant2.GND
  N5: L298N1.5V#9, L298N1.ENA
  N6: L298N1.5V#10, L298N1.ENB
  N7: L298N1.IN1, Composant1.D12/MISO
  N8: L298N1.IN3, Composant1.D11_PWM/MOSI
  N9: L298N2.OUT1, M2.pin_1
  N10: L298N2.OUT2, M2.pin_2
  N11: L298N2.OUT3, LED1.anode
  N12: L298N2.OUT4, LED1.cathode
  N13: L298N2.5V#9, L298N2.ENA
  N14: L298N2.5V#10, L298N2.ENB
  N15: L298N2.IN1, Composant1.D10_PWM/SS
  N16: L298N2.IN4, Composant1.D9_PWM
  N17: L298N3.OUT1, LED2.cathode
  N18: L298N3.OUT2, LED2.anode
  N19: L298N3.OUT3, LED3.anode
  N20: L298N3.OUT4, LED3.cathode
  N21: L298N3.5V#9, L298N3.ENA
  N22: L298N3.5V#10, L298N3.ENB
  N23: L298N3.IN1, Composant1.D8
  N24: L298N3.IN4, Composant1.D7
  N25: Composant1.D0/RX, Composant2.Tx
  N26: Composant1.D1/TX, Composant2.Rx
  5V: Composant1.5V, Composant2.VCC

custom parts:
  L298N DC motor driver: 2x DC motor driver with 78M05 positive voltage regulator (7..35 V) L298N: max 46 V, 2 A Set 5 V Enable jumper to enable 5 V regultor (needed for the L298N) and +5 V output at screw terminal or supply external +5 V at screw terminal Set ENA and/or ENB to +5 V to enable motor permanently or supply ENA and/or ENB with PWM signal IN1 and IN2 set rotation directory for motor A (OUT1/OUT2) IN2 and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
  Nextion LCD DRAFT: Nextion HMI 2.4" TFT 320x240 resistive Lcd touch screen Intelligent Display Module for Arduino NX3224T024 4M Flash, 2KByte RAM, 65k colors
